# Fritzing sketch 接线图 (saved by Fritzing 1.0.1rc)
breadboards: 4

parts:
  U1 = LuaNode32 / ESP32 [part_number=ESP32S-PIN30]
  元件1 = Adafruit RFM9x LoRa Radio [part_number="Adafruit #3072 and #3073"]
  DHT1 = DHT11 Humitidy and Temperature Sensor (3 pins)
  元件2 = Adafruit RFM9x LoRa Radio [part_number="Adafruit #3072 and #3073"]
  U2 = LuaNode32 / ESP32 [part_number=ESP32S-PIN30]

nets:
  N1: U1.D27, 元件1.DIO0
  N2: U1.D12, DHT1.Signal
  N3: U1.D13, 元件1.RST
  GND: U1.GND, 元件1.GND, DHT1.Plus
  VIN: U1.Vin, 元件1.VIN, 元件1.EN, DHT1.Gnd
  N4: U1.D5, 元件1.CS
  N5: U1.D18, 元件1.SCK
  N6: U1.D19, 元件1.MISO
  N7: U1.D23, 元件1.MOSI
  VIN_2: 元件2.VIN, 元件2.EN, U2.Vin
  GND_2: 元件2.GND, U2.GND
  N8: 元件2.DIO0, U2.D27
  N9: 元件2.SCK, U2.D18
  N10: 元件2.MISO, U2.D19
  N11: 元件2.MOSI, U2.D23
  N12: 元件2.CS, U2.D5
  N13: 元件2.RST, U2.D13

notes:
  发射端
  接收端

custom parts:
  LuaNode32 / ESP32: New Image for LuaNode32 DOIT ESP32 DEVKIT V1. Base parts from LuaNode32 / ESP32 ESP32 based LuaNode32 by G.Noorlander DOIT Esp32 DevKit v1 (30 pins long, 11 pins width) by Werner Rothschopf (modified by vanepp Dec 2018)
  Adafruit RFM9x LoRa Radio: Sending data over long distances is like magic, and now you can be a magician with this range of powerful and easy-to-use radio modules. Sure, sometimes you want to talk to a computer (a good time to use WiFi) or perhaps communicate with a Phone (choose Bluetooth Low Energy!) but what if you want to send data very far? Most WiFi, Bluetooth, Zigbee and other wireless chipsets use 2.4GHz, which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
  DHT11 Humitidy and Temperature Sensor (3 pins): DHT11 Humidity and Temperature Sensor (3 pins).
